// Logisim project 微型机.circ as structural Verilog: 7 circuits, main circuit Time 04
module Time_04 (
  input  Clock,
  input  RSet,
  output T0,
  output T1,
  output T2,
  output T3
);

  D_Flip_Flop #(.trigger("falling")) d_ff_1 (.clk(Clock), .D(T3), .Q(T0), .preset(RSet));  // open: Qn, en, reset
  D_Flip_Flop #(.trigger("falling")) d_ff_2 (.clk(Clock), .D(T0), .Q(T1), .reset(RSet));  // open: Qn, preset, en
  D_Flip_Flop #(.trigger("falling")) d_ff_3 (.clk(Clock), .D(T1), .Q(T2), .reset(RSet));  // open: Qn, preset, en
  D_Flip_Flop #(.trigger("falling")) d_ff_4 (.clk(Clock), .D(T2), .Q(T3), .reset(RSet));  // open: Qn, preset, en
endmodule

module Time_03 (
  input  Clock,
  input  RSet,
  output T0,
  output T1,
  output T2
);

  D_Flip_Flop d_ff_1 (.clk(Clock), .D(T2), .Q(T0), .preset(RSet));  // open: Qn, en, reset
  D_Flip_Flop d_ff_2 (.clk(Clock), .D(T0), .Q(T1), .reset(RSet));  // open: Qn, preset, en
  D_Flip_Flop d_ff_3 (.clk(Clock), .D(T1), .Q(T2), .reset(RSet));  // open: Qn, preset, en

  // Notes on the sheet:
  //   CLK
  //   T0
  //   T1
  //   T2
  //   时序关系示意图
endmodule

module Time_02 (
  input  Clock,
  input  RSet,
  output T0,
  output T1
);

  D_Flip_Flop #(.trigger("falling")) d_ff_1 (.clk(Clock), .D(T1), .Q(T0), .preset(RSet));  // open: Qn, en, reset
  D_Flip_Flop #(.trigger("falling")) d_ff_2 (.clk(Clock), .D(T0), .Q(T1), .reset(RSet));  // open: Qn, preset, en
endmodule

module main (
  input  in_1
);

  wire _0__G, _0__SUB, _1__SUB, _1__W, ACC_X__ACC, Ad__MAR, Ad__PC, CLK, clock_1_out,
       controlled_buffer_2_out, controlled_buffer_3_out, controlled_buffer_5_out, controlled_buffer_9_out,
       controlled_buffer_11_out, controlled_buffer_12_out, controlled_buffer_15_out,
       controlled_buffer_20_out, controlled_buffer_21_out, controlled_buffer_26_out, count_minus_minus, EX,
       FE, G, JNZ, K, L__R, M_MAR___MDR, MDR__ACC, MDR__IR, MDR__X, not_1_out, not_2_out, or_1_out, or_2_out,
       or_3_out, or_4_out, or_5_out, or_6_out, or_7_out, PC__MAR, PC_plus_plus, SUB, T0, T1, T2, T3, W;
  wire [2:0] OP;
  wire [3:0] controlled_buffer_16_out, IR_q;
  wire [7:0] ACC, BUS, controlled_buffer_4_out, controlled_buffer_7_out, controlled_buffer_8_out,
       controlled_buffer_18_out, controlled_buffer_25_out, count_q, MAR_q, MDR_q, PC_q, ram_1_data,
       shifter_1_out, X, \加or减_1_out_4 ;

  Clock clock_1 (.out(clock_1_out));
  assign CLK = G ? clock_1_out : 1'bz;  // Controlled_Buffer controlled_buffer_1
  Counter count (.load(1'b1), .count(1'b1), .Q(count_q), .clk(controlled_buffer_2_out), .clr(in_1));  // open: D, carry
  assign controlled_buffer_2_out = count_minus_minus ? CLK : 1'bz;  // Controlled_Buffer controlled_buffer_2
  CU cu_1 (
    .PC__MAR(PC__MAR), .T0(T0), .T1(T1), .T2(T2), .T3(T3), .FE(FE), .EX(EX), .M_MAR___MDR(M_MAR___MDR),
    .MDR__IR(MDR__IR), .PC_plus_plus(PC_plus_plus), .OP(OP), .Ad__MAR(Ad__MAR), .MDR__ACC(MDR__ACC),
    .MDR__X(MDR__X), ._0__SUB(_0__SUB), .ACC_X__ACC(ACC_X__ACC), ._1__SUB(_1__SUB), .L__R(L__R),
    ._1__W(_1__W), .count_minus_minus(count_minus_minus), .Ad__PC(Ad__PC), ._0__G(_0__G), .X(K), .out_24(W));
  Time_04 time_04_1 (.Clock(CLK), .RSet(in_1), .T0(T0), .T1(T1), .T2(T2), .T3(T3));
  Comparator comparator_1 (.a(count_q), .b({8{1'b0}}), .gt(JNZ));  // open: eq, lt
  Time_02 time_02_1 (.Clock(T3), .RSet(in_1), .T0(FE), .T1(EX));
  assign controlled_buffer_3_out = JNZ ? Ad__PC : 1'bz;  // Controlled_Buffer controlled_buffer_3
  Counter PC (
    .load(controlled_buffer_3_out), .D(BUS), .count(PC_plus_plus), .Q(PC_q), .clk(CLK), .clr(in_1));  // open: carry
  assign controlled_buffer_4_out = or_1_out ? BUS : 8'bz;  // Controlled_Buffer controlled_buffer_4
  or or_1 (or_1_out, PC__MAR, Ad__MAR);
  assign controlled_buffer_5_out = or_1_out ? CLK : 1'bz;  // Controlled_Buffer controlled_buffer_5
  assign BUS = PC__MAR ? PC_q : 8'bz;  // Controlled_Buffer controlled_buffer_6
  Register MAR (.D(controlled_buffer_4_out), .Q(MAR_q), .clk(controlled_buffer_5_out), .clr(in_1));  // open: en
  or or_2 (or_2_out, MDR__ACC, L__R);
  assign controlled_buffer_7_out = MDR__IR ? BUS : 8'bz;  // Controlled_Buffer controlled_buffer_7
  assign controlled_buffer_8_out = or_2_out ? BUS : 8'bz;  // Controlled_Buffer controlled_buffer_8
  or or_3 (or_3_out, or_2_out, ACC_X__ACC);
  \加or减  \u_加or减_1  (.ACC(ACC), .X(X), .out_4(\加or减_1_out_4 ), .SUB(SUB));
  assign controlled_buffer_9_out = _0__SUB ? 1'b0 : 1'bz;  // Controlled_Buffer controlled_buffer_9
  assign controlled_buffer_9_out = _1__SUB ? 1'b1 : 1'bz;  // Controlled_Buffer controlled_buffer_10
  Register IR (.D(controlled_buffer_7_out), .Q({OP, K, IR_q}), .clk(controlled_buffer_11_out), .clr(in_1));  // open: en
  assign controlled_buffer_11_out = MDR__IR ? CLK : 1'bz;  // Controlled_Buffer controlled_buffer_11
  RAM #(.bus("asynch")) ram_1 (.addr(MAR_q), .data(ram_1_data), .ld(not_1_out));  // open: sel, clr
  not not_1 (not_1_out, _1__W);
  Register u_ACC (.D(controlled_buffer_8_out), .Q(ACC), .clk(controlled_buffer_12_out), .clr(in_1));  // open: en
  assign controlled_buffer_12_out = or_3_out ? CLK : 1'bz;  // Controlled_Buffer controlled_buffer_12
  assign controlled_buffer_8_out = ACC_X__ACC ? \加or减_1_out_4  : 8'bz;  // Controlled_Buffer controlled_buffer_13
  assign BUS = L__R ? shifter_1_out : 8'bz;  // Controlled_Buffer controlled_buffer_14
  Shifter #(.shift("lr")) shifter_1 (.in(ACC), .\dist (3'b001), .out(shifter_1_out));
  Register #(.width(1)) u_SUB (
    .D(controlled_buffer_9_out), .Q(SUB), .clk(controlled_buffer_15_out), .clr(in_1));  // open: en
  assign controlled_buffer_15_out = or_4_out ? CLK : 1'bz;  // Controlled_Buffer controlled_buffer_15
  or or_4 (or_4_out, _1__SUB, _0__SUB);
  assign controlled_buffer_16_out = not_2_out ? 4'b1010 : 4'bz;  // Controlled_Buffer controlled_buffer_16
  not not_2 (not_2_out, W);
  assign ram_1_data = _1__W ? ACC : 8'bz;  // Controlled_Buffer controlled_buffer_17
  assign controlled_buffer_18_out = not_1_out ? ram_1_data : 8'bz;  // Controlled_Buffer controlled_buffer_18
  assign controlled_buffer_16_out = W ? 4'b0000 : 4'bz;  // Controlled_Buffer controlled_buffer_19
  Register MDR (.D(controlled_buffer_18_out), .Q(MDR_q), .clk(controlled_buffer_20_out), .clr(in_1));  // open: en
  assign controlled_buffer_20_out = M_MAR___MDR ? CLK : 1'bz;  // Controlled_Buffer controlled_buffer_20
  assign controlled_buffer_21_out = _0__G ? 1'b0 : 1'bz;  // Controlled_Buffer controlled_buffer_21
  assign controlled_buffer_21_out = in_1 ? 1'b1 : 1'bz;  // Controlled_Buffer controlled_buffer_22
  assign BUS = or_5_out ? {controlled_buffer_16_out, IR_q} : 8'bz;  // Controlled_Buffer controlled_buffer_23
  or or_5 (or_5_out, Ad__MAR, Ad__PC);
  assign BUS = or_6_out ? MDR_q : 8'bz;  // Controlled_Buffer controlled_buffer_24
  or or_6 (or_6_out, MDR__IR, MDR__X, MDR__ACC);
  assign controlled_buffer_25_out = MDR__X ? BUS : 8'bz;  // Controlled_Buffer controlled_buffer_25
  assign controlled_buffer_26_out = MDR__X ? CLK : 1'bz;  // Controlled_Buffer controlled_buffer_26
  Register #(.width(1)) u_G (.D(controlled_buffer_21_out), .Q(G), .clk(or_7_out));  // open: en, clr
  or or_7 (or_7_out, in_1, _0__G);
  Register u_X (.D(controlled_buffer_25_out), .Q(X), .clk(controlled_buffer_26_out), .clr(in_1));  // open: en
  Hex_Digit_Display hex_digit_display_1 (.value(ACC[7:4]));  // open: dp
  Hex_Digit_Display hex_digit_display_2 (.value(ACC[3:0]));  // open: dp

  // Other names for the same wires on the sheet: RST = in_1
endmodule

module CU (
  input  T0,
  input  T1,
  input  T2,
  input  T3,
  input  FE,
  input  EX,
  input  [2:0] OP,
  input  X,
  output M_MAR___MDR,
  output PC__MAR,
  output MDR__IR,
  output PC_plus_plus,
  output Ad__MAR,
  output MDR__ACC,
  output MDR__X,
  output _0__SUB,
  output ACC_X__ACC,
  output _1__SUB,
  output L__R,
  output _1__W,
  output count_minus_minus,
  output Ad__PC,
  output _0__G,
  output out_24
);

  wire ADD, and_2_out, and_3_out, DEC, LDA, or_2_out, or_3_out, or_4_out, or_5_out, SHR, STA, STOP, SUB;

  and and_1 (PC__MAR, T0, FE);
  Decoder #(.select(3)) decoder_1 (
    .out0(LDA), .out1(ADD), .out2(SUB), .out3(SHR), .out4(STA), .out5(DEC), .out6(out_24), .out7(STOP),
    .sel(OP));  // open: en
  or or_1 (M_MAR___MDR, and_2_out, and_3_out);
  and and_2 (and_2_out, T1, FE);
  and and_3 (and_3_out, T1, or_2_out, EX);
  or or_2 (or_2_out, LDA, SUB, ADD);
  and and_4 (MDR__IR, T2, FE);
  and and_5 (PC_plus_plus, T3, FE);
  and and_6 (count_minus_minus, T2, DEC, EX);
  and and_7 (Ad__MAR, T0, or_3_out, EX);
  or or_3 (or_3_out, LDA, SUB, STA, ADD);
  and and_8 (MDR__ACC, T2, LDA, EX);
  and and_9 (Ad__PC, T2, out_24, EX);
  and and_10 (MDR__X, T2, or_4_out, EX);
  or or_4 (or_4_out, ADD, SUB);
  and and_11 (_0__G, T3, STOP, EX);
  and and_12 (_0__SUB, T2, ADD, EX);
  and and_13 (ACC_X__ACC, T3, or_5_out, EX);
  or or_5 (or_5_out, ADD, SUB);
  and and_14 (_1__SUB, T2, SUB, EX);
  and and_15 (L__R, T2, SHR, EX);
  and and_16 (_1__W, T1, STA, EX);

  // Other names for the same wires on the sheet: JNZ = out_24
endmodule

module \加or减  (
  input  [7:0] ACC,
  input  [7:0] X,
  input  SUB,
  output [7:0] out_4
);

  wire [7:0] adder_1_out, subtractor_1_out;

  Adder adder_1 (.a(ACC), .b(X), .out(adder_1_out));  // open: cin, cout
  Subtractor subtractor_1 (.a(ACC), .b(X), .out(subtractor_1_out));  // open: bin, bout
  Multiplexer #(.width(8)) multiplexer_1 (
    .in0(adder_1_out), .in1(subtractor_1_out), .out(out_4), .sel(SUB));  // open: en
endmodule

module graph (
  input  MDRoutE,
  input  MDRout,
  input  Xout,
  input  PCout,
  input  LRout,
  input  CompareOut,
  input  PC_1,
  input  ACC__ALU,
  input  ALU__ACC,
  input  BUS__ACC,
  input  ACC__BUS,
  input  ACC__LR
);

  wire controlled_buffer_1_out, controlled_buffer_6_out, controlled_buffer_7_out, undriven;

  assign controlled_buffer_1_out = Xout ? controlled_buffer_1_out : 1'bz;  // Controlled_Buffer controlled_buffer_1
  assign controlled_buffer_1_out = CompareOut ? undriven : 1'bz;  // Controlled_Buffer controlled_buffer_2
  assign controlled_buffer_1_out = LRout ? controlled_buffer_7_out : 1'bz;  // Controlled_Buffer controlled_buffer_3
  assign controlled_buffer_1_out = ACC__ALU ? controlled_buffer_6_out : 1'bz;  // Controlled_Buffer controlled_buffer_4
  assign controlled_buffer_1_out = ACC__BUS ? controlled_buffer_6_out : 1'bz;  // Controlled_Buffer controlled_buffer_5
  assign controlled_buffer_6_out = ALU__ACC ? controlled_buffer_1_out : 1'bz;  // Controlled_Buffer controlled_buffer_6
  assign controlled_buffer_7_out = ACC__LR ? controlled_buffer_6_out : 1'bz;  // Controlled_Buffer controlled_buffer_7
  assign controlled_buffer_6_out = BUS__ACC ? controlled_buffer_1_out : 1'bz;  // Controlled_Buffer controlled_buffer_8
  assign controlled_buffer_1_out = MDRoutE ? controlled_buffer_1_out : 1'bz;  // Controlled_Buffer controlled_buffer_9
  assign controlled_buffer_1_out = MDRout ? controlled_buffer_1_out : 1'bz;  // Controlled_Buffer controlled_buffer_10
  assign controlled_buffer_1_out = PC_1 ? controlled_buffer_1_out : 1'bz;  // Controlled_Buffer controlled_buffer_11
  assign controlled_buffer_1_out = PCout ? controlled_buffer_1_out : 1'bz;  // Controlled_Buffer controlled_buffer_12

  // Notes on the sheet:
  //   Count--
  //   Xin
  //   Count
  //   X
  //   MARin
  //   MAR
  //   Compare
  //   ValueIn
  //   MemR
  //   L->R
  //   M
  //   MemW
  //   Data
  //   ALU
  //   ACC
  //   Addr
  //   MDRin
  //   MDR
  //   0->SUB
  //   SUB
  //   1->SUB
  //   MDRinE
  //   PC
  //   Ad(IR)out
  //   IR
  //   至指令译码部件
  //   CB
  //   DB
  //   AB
  //   BUS
  //   PCin
  //   IRin
  //   微操作
  //   PC->MAR
  //   M[MAR]->MDR
  //   MDR->IR
  //   PC+1->PC
  //   Ad(IR)->MAR
  //   MDR->ACC
  //   MDR->X
  //   ACC+X->ACC
  //   ACC->MDR
  //   MDR->M[MAR]
  //   有效控制信号
  //   PCout,MARin
  //   MemR,MDRinE
  //   MDRout,IRin
  //   PC+1
  //   Ad(IR)out,MARin
  //   MDRout,BUS->ACC
  //   MDRout,Xin
  //   Xout,ACC->ALU,0->SUBALU->ACC
  //   ACC->BUS,MDRin
  //   MDRoutE,MemW
endmodule
