// Logisim project 补码一位乘.circ as structural Verilog: 7 circuits, main circuit 补码一位乘
module \补码一位乘  (
  input  [7:0] in_1,
  input  [7:0] in_2,
  input  in_3,
  input  in_4
);

  wire clock_1_out, \continue , controlled_buffer_2_out, K, \高位右移_1_out_2 ;
  wire [3:0] \结果处理_1_out_3_2 ;
  wire [7:0] counter_1_q, multiplier_1_cout, multiplier_1_out;
  wire [8:0] ACC, contral_1_out_4, controlled_buffer_1_out, MQ, \低位右移_1_out_3 , \加法器_1_out_3 , \高位右移_1_out_3 ;
  wire [15:0] \结果处理_1_out_3 ;

  Multiplier multiplier_1 (.a(in_1), .b(in_2), .out(multiplier_1_out), .cout(multiplier_1_cout));  // open: cin
  Hex_Digit_Display hex_digit_display_1 (.value(multiplier_1_cout[7:4]));  // open: dp
  Hex_Digit_Display hex_digit_display_2 (.value(multiplier_1_cout[3:0]));  // open: dp
  Hex_Digit_Display hex_digit_display_3 (.value(multiplier_1_out[3:0]));  // open: dp
  Hex_Digit_Display hex_digit_display_4 (.value(multiplier_1_out[7:4]));  // open: dp
  \高位右移  \u_高位右移_1  (.in_1(\加法器_1_out_3 ), .out_2(\高位右移_1_out_2 ), .out_3(\高位右移_1_out_3 ));
  \加法器  \u_加法器_1  (.out_3(\加法器_1_out_3 ), .in_1(ACC), .in_2(contral_1_out_4));
  contral contral_1 (.in_1(MQ[1]), .in_2(MQ[0]), .out_4(contral_1_out_4), .in_3(in_1));
  Register #(.width(9)) u_ACC (.D(\高位右移_1_out_3 ), .Q(ACC), .clk(controlled_buffer_2_out), .clr(in_3));  // open: en
  assign controlled_buffer_1_out = K ? \低位右移_1_out_3  : 9'bz;  // Controlled_Buffer controlled_buffer_1
  \低位右移  \u_低位右移_1  (.out_3(\低位右移_1_out_3 ), .in_1(\高位右移_1_out_2 ), .in_2(MQ));
  Register #(.width(9)) u_MQ (
    .D(controlled_buffer_1_out), .Q(MQ), .clk(controlled_buffer_2_out), .clr(in_3));  // open: en
  assign controlled_buffer_2_out = \continue  ? clock_1_out : 1'bz;  // Controlled_Buffer controlled_buffer_2
  Counter counter_1 (.Q(counter_1_q), .clk(controlled_buffer_2_out), .clr(in_3));  // open: load, D, count, carry
  Clock clock_1 (.out(clock_1_out));
  \结果处理  \u_结果处理_1  (.in_1(ACC), .in_2(MQ), .out_3({\结果处理_1_out_3 [15:8], \结果处理_1_out_3_2 , \结果处理_1_out_3 [3:0]}));
  Comparator comparator_1 (.a(counter_1_q), .b(8'h8), .lt(\continue ));  // open: gt, eq
  Comparator comparator_2 (.a(counter_1_q), .b(8'h7), .lt(K));  // open: gt, eq
  Hex_Digit_Display hex_digit_display_5 (.value(\结果处理_1_out_3 [11:8]));  // open: dp
  Hex_Digit_Display hex_digit_display_6 (.value(\结果处理_1_out_3 [15:12]));  // open: dp
  Hex_Digit_Display hex_digit_display_7 (.value(\结果处理_1_out_3_2 ));  // open: dp
  Hex_Digit_Display hex_digit_display_8 (.value(\结果处理_1_out_3 [3:0]));  // open: dp

  // Other names for the same wires on the sheet: LA = in_4; R1 = MQ[0]; R0 = MQ[1]; RST = in_3; X[7:0] = in_1;
  //   Y[7:0] = in_2

  // Notes on the sheet:
  //   11111110x1fa
  //   加8次移7次
endmodule

module contral (
  input  in_1,
  input  in_2,
  input  [7:0] in_3,
  output [8:0] out_4
);

  wire [7:0] \x补_1_out_2 ;

  \x补  \x补_1  (.out_2(\x补_1_out_2 ), .in_1(in_3));
  Multiplexer #(.select(2), .width(9)) multiplexer_1 (
    .in0({9{1'b0}}), .in1({{2{\x补_1_out_2 [7]}}, \x补_1_out_2 [6:0]}), .in2({{2{in_3[7]}}, in_3[6:0]}),
    .in3({9{1'b0}}), .out(out_4), .sel({in_2, in_1}));  // open: en

  // Other names for the same wires on the sheet: R0 = in_1; R1 = in_2
endmodule

module \x补  (
  input  [7:0] in_1,
  output [7:0] out_2
);

  wire [7:0] not_1_out;

  assign not_1_out = ~in_1;  // NOT_Gate not_1, 8 bits wide
  Adder adder_1 (.a({8{1'b0}}), .b(not_1_out), .out(out_2), .cin(1'b1));  // open: cout
endmodule

module \加法器  (
  input  [8:0] in_1,
  input  [8:0] in_2,
  output [8:0] out_3
);

  Adder #(.width(9)) adder_1 (.a(in_1), .b(in_2), .out(out_3));  // open: cin, cout
endmodule

module \高位右移  (
  input  [8:0] in_1,
  output out_2,
  output [8:0] out_3
);

  Shifter #(.width(9), .shift("ar")) shifter_1 (.in(in_1), .\dist (4'b0001), .out(out_3));

  assign out_2 = in_1[0];
endmodule

module \低位右移  (
  input  in_1,
  input  [8:0] in_2,
  output [8:0] out_3
);


  assign out_3 = {in_1, in_2[8:1]};
endmodule

module \结果处理  (
  input  [8:0] in_1,
  input  [8:0] in_2,
  output [15:0] out_3
);


  assign out_3 = {in_1, in_2[8:2]};

  // Notes on the sheet:
  //   高位
  //   低位
endmodule
